# Fritzing sketch BLEconnectionTFTnano (saved by Fritzing 0.9.3b)
breadboards: 1

parts:
  TFT1 = 1.8" TFT Display with uSD
  Part4 = Arduino Nano (Rev3.0)
  Part5 = Bluetooth HM-10

nets:
  N1: TFT1.BLK, Part4.3V3
  N2: TFT1.CS, Part4.D10
  N3: TFT1.DC, Part4.D9
  N4: TFT1.RST, Part4.D8
  N5: TFT1.SDA, Part4.D11/MOSI
  N6: TFT1.SCL, Part4.D13/SCK
  VCC: TFT1.VCC, Part4.5V, Part5.VCC
  GND: TFT1.GND, Part4.GND, Part5.GND
  N7: Part4.D2, Part5.TXD
  N8: Part4.D3, Part5.RXD

custom parts:
  1.8" TFT Display with uSD: 1.8" TFT Display with SPI control and MicroSD card
