# Fritzing sketch BTconnectionTFTnano (saved by Fritzing 0.9.3b)
breadboards: 1

parts:
  TFT1 = 1.8" TFT Display with uSD
  Part3 = Bluetooth HC-05 Macho
  Part4 = Arduino Nano (Rev3.0)
  R1 = Resistor [tolerance=±5% resistance=220 package=THT]
  R2 = Resistor [tolerance=±5% resistance=100 package="2512 [SMD]"]

nets:
  N1: TFT1.BLK, Part4.3V3
  N2: TFT1.CS, Part4.D10
  N3: TFT1.DC, Part4.D9
  N4: TFT1.RST, Part4.D8
  N5: TFT1.SDA, Part4.D11/MOSI
  N6: TFT1.SCL, Part4.D13/SCK
  VCC: TFT1.VCC, Part3.VCC, Part4.5V
  GND: TFT1.GND, Part3.GND, Part4.GND, R1.Pin_1
  N7: Part3.TXD, Part4.D2
  N8: Part3.RXD, R1.Pin_0, R2.Pin_1
  N9: Part4.D3, R2.Pin_0

custom parts:
  1.8" TFT Display with uSD: 1.8" TFT Display with SPI control and MicroSD card
