# Fritzing sketch TFTDisplayText (saved by Fritzing 0.9.3b)
breadboards: 1

parts:
  Part1 = Arduino Uno (Rev3)
  Part2 = Humidity Sensor - HIH-4030 Breakout
  TFT1 = 1.8" TFT Display with uSD

nets:
  GND: Part1.A0, Part1.GND, Part2.GND, Part2.OUT, TFT1.GND
  N1: Part1.D8, TFT1.RST
  N2: Part1.D9_PWM, TFT1.DC
  N3: Part1.D10_PWM/SS, TFT1.CS
  N4: Part1.D11_PWM/MOSI, TFT1.SDA
  N5: Part1.D13/SCK, TFT1.SCL
  N6: Part1.ioref, Part2.VCC
  N7: Part1.3V3, TFT1.BLK
  5V: Part1.5V, TFT1.VCC

custom parts:
  1.8" TFT Display with uSD: 1.8" TFT Display with SPI control and MicroSD card
