# Fritzing sketch coboBTLedTest (saved by Fritzing 0.9.3b)
breadboards: 1

parts:
  Part1 = Arduino Uno (Rev3)
  Part2 = Bluetooth HC-05 Macho
  LED1 = LED - 3mm [color="Red (633nm)" package="3 mm [THT]"]

nets:
  N1: Part1.D12/MISO, LED1.anode
  N2: Part1.D2, Part2.TXD
  N3: Part1.D3_PWM, Part2.RXD
  5V: Part1.5V, Part2.VCC
  GND: Part1.GND, Part2.GND, LED1.cathode
